# Fritzing sketch mazesolving (saved by Fritzing 0.9.3b)

parts:
  Part1 = Arduino Uno (Rev3)
  Part3 = 9-DOF Absolute Orientation IMU Fusion Breakout - BNO055
  M1 = DC Motor
  M2 = DC Motor
  hc-sr1 = hc-sr04
  hc-sr2 = hc-sr04
  hc-sr3 = hc-sr04
  BATT1 = LiPoly Battery (1300mAh)
  Part2 = Arduino Motor Shield

nets:
  N1: Part1.D9_PWM, hc-sr2.Trig
  N2: Part1.D10_PWM/SS, hc-sr2.Echo
  N3: Part1.A4/SDA, Part3.SDA_5V
  N4: Part1.A5/SCL, Part3.SCL_5V
  N5: Part1.D4, hc-sr1.Echo
  N6: Part1.D5_PWM, hc-sr1.Trig
  N7: Part1.D6_PWM, hc-sr3.Trig
  N8: Part1.D7, hc-sr3.Echo
  5V: Part1.5V, Part2.5V, Part2.N$394
  GND: Part1.GND, BATT1.negative, Part2.GND, Part2.N$287
  N9: Part1.VIN, BATT1.positive
  N10: Part3.5.0V, Part2.N$398
  N11: Part3.GND, Part2.N$313
  N12: M1.pin_1, Part2.OUT2
  N13: M1.pin_2, Part2.OUT1
  N14: M2.pin_1, Part2.OUT3
  N15: M2.pin_2, Part2.OUT4
  N16: hc-sr1.VCC, Part2.N$396
  N17: hc-sr1.GND, Part2.N$261
  N18: hc-sr2.VCC, Part2.N$395
  N19: hc-sr2.GND, Part2.N$235
  N20: hc-sr3.VCC, Part2.N$397
  N21: hc-sr3.GND, Part2.N$209

custom parts:
  9-DOF Absolute Orientation IMU Fusion Breakout - BNO055: A MEMS accelerometer, magnetometer and gyroscope on a single die with a high speed ARM Cortex-M0 based processor to digest all the sensor data, abstract the sensor fusion and real time requirements away, and spit out data you can use in quaternions, Euler angles or vectors.
  LiPoly Battery (1300mAh): Lithium Ion Polymer Battery (1300mAh)
